# Fritzing sketch ThermoHome_pi (saved by Fritzing 0.9.4)
breadboards: 1

parts:
  RHT1 = Humidity and Temperature Sensor RHT03
  R1 = Resistor [tolerance=±5% resistance=220 package=THT]
  WeMos_D1_Mini_Relay_Shield_V1 = WeMos D1 Mini Relay Shield V2  # not connected
  Raspberry_Pi_1 = Raspberry Pi 3 [part_number=RPI-3-V1.2]

nets:
  VCC: RHT1.Vcc, R1.Pin_1, Raspberry_Pi_1.5V
  N1: RHT1.Data-signal, R1.Pin_0, Raspberry_Pi_1.GPIO4
  N2: RHT1.GND_2, Raspberry_Pi_1.GND
